# Fritzing sketch sequencino (saved by Fritzing 0.9.1b)
breadboards: 2

parts:
  S2 = Pushbutton [package="[THT]"]
  S2_2 = Pushbutton [package="[THT]"]
  R3 = Resistor [resistance=1k tolerance=±5% package=THT]
  R3_2 = Resistor [resistance=1k tolerance=±5% package=THT]
  R3_3 = Resistor [resistance=1k tolerance=±5% package=THT]
  R3_4 = Resistor [resistance=1k tolerance=±5% package=THT]
  R3_5 = Resistor [resistance=1k tolerance=±5% package=THT]
  R3_6 = Resistor [resistance=1k tolerance=±5% package=THT]
  R3_7 = Resistor [resistance=1k tolerance=±5% package=THT]
  R3_8 = Resistor [resistance=1k tolerance=±5% package=THT]
  R3_9 = Resistor [resistance=1k tolerance=±5% package=THT]
  R3_10 = Resistor [resistance=1k tolerance=±5% package=THT]
  DIN1 = DIN-5 jack (MIDI) [package=THT]
  R4 = Resistor [resistance=220 tolerance=±5% package=THT]
  R5 = Resistor [resistance=10k tolerance=±5% package=THT]
  R5_2 = Resistor [resistance=10k tolerance=±5% package=THT]
  LED3 = LED - 5mm [color="Yellow (585nm)" package="5 mm [THT]"]
  LED5 = LED - 5mm [color="Yellow (585nm)" package="5 mm [THT]"]
  LED8 = LED - 5mm [color="Yellow (585nm)" package="5 mm [THT]"]
  LED1 = LED - 5mm [color="Yellow (585nm)" package="5 mm [THT]"]
  LED6 = LED - 5mm [color="Yellow (585nm)" package="5 mm [THT]"]
  LED10 = LED - 5mm [color="Red (633nm)" package="5 mm [THT]"]
  LED4 = LED - 5mm [color="Yellow (585nm)" package="5 mm [THT]"]
  R2 = Rotary Potentiometer (Small) [maximum_resistance=100kΩ package=THT]  # not connected
  LED2 = LED - 5mm [color="Yellow (585nm)" package="5 mm [THT]"]
  LED7 = LED - 5mm [color="Yellow (585nm)" package="5 mm [THT]"]
  Arduino1 = Arduino Uno (Rev3)
  LED9 = LED - 5mm [color="Green (555nm)" package="5 mm [THT]"]
  DIN2 = DIN-5 jack (MIDI) [package=THT]
  IC1 = IC, DIP package, 8 pins [chip_label=IC]
  R6 = Resistor [tolerance=±5% resistance=220 package=THT]
  D1 = Rectifier Diode [part_number=1N4001 package="300 mil [THT]"]
  R7 = Resistor [tolerance=±5% resistance=10k package=THT]
  R8 = Resistor [tolerance=±5% resistance=470 package=THT]

nets (from the breadboard view):
  N1: S2.Pin_1, S2.Pin_2, S2_2.Pin_1, S2_2.Pin_2, R4.Pin_1, Arduino1.5V, IC1.pin8, R8.Pin_0
  N2: S2.Pin_3, S2.Pin_4, R5_2.Pin_0, Arduino1.A0
  N3: S2_2.Pin_3, S2_2.Pin_4, R5.Pin_0, Arduino1.A1
  N4: R3.Pin_0, LED10.cathode
  N5: R3.Pin_1, R3_2.Pin_1, R3_3.Pin_1, R3_4.Pin_1, R3_5.Pin_1, R3_6.Pin_1, R3_7.Pin_1, R3_8.Pin_1, R3_9.Pin_1, R3_10.Pin_1, DIN1.2, R5.Pin_1, R5_2.Pin_1, Arduino1.GND, IC1.pin5, R7.Pin_1
  N6: R3_2.Pin_0, LED9.cathode
  N7: R3_3.Pin_0, LED8.cathode
  N8: R3_4.Pin_0, LED7.cathode
  N9: R3_5.Pin_0, LED6.cathode
  N10: R3_6.Pin_0, LED5.cathode
  N11: R3_7.Pin_0, LED4.cathode
  N12: R3_8.Pin_0, LED3.cathode
  N13: R3_9.Pin_0, LED2.cathode
  N14: R3_10.Pin_0, LED1.cathode
  N15: DIN1.5, Arduino1.D1/TX
  N16: DIN1.4, R4.Pin_0
  N17: LED3.anode, Arduino1.D11_PWM/MOSI
  N18: LED5.anode, Arduino1.D9_PWM
  N19: LED8.anode, Arduino1.D6_PWM
  N20: LED1.anode, Arduino1.D13/SCK
  N21: LED6.anode, Arduino1.D8
  N22: LED10.anode, Arduino1.D4
  N23: LED4.anode, Arduino1.D10_PWM/SS
  N24: LED2.anode, Arduino1.D12/MISO
  N25: LED7.anode, Arduino1.D7
  N26: Arduino1.D0/RX, IC1.pin6, R8.Pin_1
  N27: Arduino1.D5_PWM, LED9.anode
  N28: DIN2.5, R6.Pin_0
  N29: DIN2.4, IC1.pin2, D1.cathode
  N30: IC1.pin3, R6.Pin_1, D1.anode
  N31: IC1.pin7, R7.Pin_0
